// Digital circuit control_bomba.dig as structural Verilog
module control_bomba (
  input  tanqueH,
  input  tanqueL,
  input  cisternaOK,
  input  cisternaL,
  input  Ck,
  output bomba
);

  wire and_1_out, not_1_out, not_2_out, not_3_out, not_4_out, not_5_out, not_6_out, not_7_out, not_8_out,
       not_9_out, not_10_out, not_11_out, not_12_out, not_13_out, or_1_out, or_2_out, or_3_out, or_4_out,
       or_5_out;

  not not_1 (not_1_out, tanqueH);
  not not_2 (not_2_out, tanqueL);
  not not_3 (not_3_out, cisternaOK);
  not not_4 (not_4_out, bomba);
  not not_5 (not_5_out, tanqueH);
  not not_6 (not_6_out, tanqueL);
  not not_7 (not_7_out, bomba);
  not not_8 (not_8_out, tanqueH);
  not not_9 (not_9_out, tanqueL);
  not not_10 (not_10_out, bomba);
  not not_11 (not_11_out, tanqueH);
  not not_12 (not_12_out, cisternaOK);
  not not_13 (not_13_out, tanqueH);
  or or_1 (or_1_out, not_1_out, not_2_out, cisternaL, not_3_out, not_4_out);
  or or_2 (or_2_out, not_5_out, not_6_out, cisternaL, cisternaOK, not_7_out);
  or or_3 (or_3_out, not_8_out, not_9_out, cisternaL, cisternaOK, not_10_out);
  or or_4 (or_4_out, not_11_out, tanqueL, cisternaL, not_12_out, bomba);
  or or_5 (or_5_out, not_13_out, tanqueL, cisternaL, cisternaOK, bomba);
  and and_1 (and_1_out, or_1_out, or_2_out, or_3_out, or_4_out, or_5_out);
  D_FF d_ff_1 (.D(and_1_out), .C(Ck), .Q(bomba));  // open: nQ
endmodule
